// Logisim project aquarium.circ as structural Verilog: 1 circuit, main circuit main
module main (
  input  A,
  input  B,
  input  C,
  input  D,
  output Z,
  output X,
  output Y
);

  wire and_1_out, and_2_out, and_3_out, and_4_out, and_5_out, and_6_out, not_1_out, not_2_out, not_3_out,
       not_4_out, not_5_out, or_1_out, or_2_out, or_3_out, or_4_out, or_5_out, or_6_out, or_7_out;

  and and_1 (and_1_out, B, A);
  not not_1 (not_1_out, C);
  and and_2 (and_2_out, B, A);
  or or_1 (or_1_out, B, A);
  not not_2 (not_2_out, D);
  and and_3 (and_3_out, C, and_1_out);
  or or_2 (or_2_out, C, B);
  not not_3 (not_3_out, D);
  and and_4 (and_4_out, not_1_out, and_2_out);
  or or_3 (or_3_out, C, B);
  or or_4 (or_4_out, C, or_1_out);
  and and_5 (and_5_out, not_2_out, and_3_out);
  or or_5 (or_5_out, D, or_2_out);
  and and_6 (and_6_out, not_3_out, and_4_out);
  or or_6 (or_6_out, D, or_3_out);
  or or_7 (or_7_out, D, or_4_out);
  not not_4 (not_4_out, or_5_out);
  not not_5 (not_5_out, or_6_out);
  not not_6 (Z, or_7_out);
  or or_8 (X, and_5_out, not_4_out);
  or or_9 (Y, and_6_out, not_5_out);
endmodule
