// Logisim project mul.circ as structural Verilog: 3 circuits, main circuit serial_mult
module shift_reg (
  input  [7:0] x,
  input  load,
  input  clk,
  output [7:0] y
);

  wire multiplexer_1_out, multiplexer_2_out, multiplexer_3_out, multiplexer_4_out, multiplexer_5_out,
       multiplexer_6_out, multiplexer_7_out, multiplexer_8_out, not_1_out, not_2_out;

  not not_1 (not_1_out, load);
  Multiplexer multiplexer_1 (.in0(x[7]), .in1(y[6]), .out(multiplexer_1_out), .sel(not_1_out));
  D_Flip_Flop d_ff_1 (.D(multiplexer_1_out), .clk(clk), .Q(y[7]));  // open: Qn, preset, reset
  Multiplexer multiplexer_2 (.in0(x[6]), .in1(y[5]), .out(multiplexer_2_out), .sel(not_1_out));
  D_Flip_Flop d_ff_2 (.D(multiplexer_2_out), .clk(clk), .Q(y[6]));  // open: Qn, preset, reset
  Multiplexer multiplexer_3 (.in0(x[5]), .in1(y[4]), .out(multiplexer_3_out), .sel(not_1_out));
  D_Flip_Flop d_ff_3 (.D(multiplexer_3_out), .clk(clk), .Q(y[5]));  // open: Qn, preset, reset
  Multiplexer multiplexer_4 (.in0(x[4]), .in1(y[3]), .out(multiplexer_4_out), .sel(not_1_out));
  D_Flip_Flop d_ff_4 (.D(multiplexer_4_out), .clk(clk), .Q(y[4]));  // open: Qn, preset, reset
  Multiplexer multiplexer_5 (.in0(x[3]), .in1(y[2]), .out(multiplexer_5_out), .sel(not_1_out));
  D_Flip_Flop d_ff_5 (.D(multiplexer_5_out), .clk(clk), .Q(y[3]));  // open: Qn, preset, reset
  Multiplexer multiplexer_6 (.in0(x[2]), .in1(y[1]), .out(multiplexer_6_out), .sel(not_1_out));
  D_Flip_Flop d_ff_6 (.D(multiplexer_6_out), .clk(clk), .Q(y[2]));  // open: Qn, preset, reset
  Multiplexer multiplexer_7 (.in0(x[1]), .in1(y[0]), .out(multiplexer_7_out), .sel(not_1_out));
  D_Flip_Flop d_ff_7 (.D(multiplexer_7_out), .clk(clk), .Q(y[1]));  // open: Qn, preset, reset
  Multiplexer multiplexer_8 (.in0(x[0]), .in1(not_2_out), .out(multiplexer_8_out), .sel(not_1_out));
  D_Flip_Flop d_ff_8 (.D(multiplexer_8_out), .clk(clk), .Q(y[0]));  // open: Qn, preset, reset
  not not_2 (not_2_out, 1'b1);
endmodule

module preprocess (
  input  [7:0] x,
  output [7:0] y
);
endmodule

module serial_mult (
  input  [3:0] a,
  input  load,
  input  [3:0] b,
  output [7:0] y
);
endmodule
