// Logisim project riscv_multi.circ as structural Verilog: 10 circuits, main circuit main
module main (
  input  Reset,
  output halt
);

  wire alu_1_zero, clk_out, controller_1_adrsrc, controller_1_irwrite, controller_1_memwrite,
       controller_1_pcwrite, controller_1_regwrite;
  wire [1:0] controller_1_alusrca, controller_1_alusrcb, controller_1_immsrc, controller_1_resultsrc;
  wire [2:0] controller_1_aluctrl;
  wire [31:0] A_q, alu_1_aluresult, ALUOut_q, B_q, Data_q, extend_1_immext, Instr_q, Mem_dout,
       multiplexer_1_out, multiplexer_2_out, multiplexer_3_out, multiplexer_4_out, OldPc_q, regfile_1_rd1,
       regfile_1_rd2, register_1_q;

  Clock clk (.out(clk_out));
  Register #(.width(32)) register_1 (
    .D(multiplexer_4_out), .en(controller_1_pcwrite), .clk(clk_out), .Q(register_1_q), .clr(Reset));
  Multiplexer #(.width(32)) multiplexer_1 (
    .in0(register_1_q), .in1(multiplexer_4_out), .out(multiplexer_1_out), .sel(controller_1_adrsrc));
  RAM #(.addrWidth(16), .asyncread("true"), .dataWidth(32)) Mem (
    .addr(multiplexer_1_out[17:2]), .we(controller_1_memwrite), .oe(1'b1), .clk(clk_out), .din(B_q),
    .dout(Mem_dout));
  Register #(.width(32)) OldPc (.D(register_1_q), .clk(clk_out), .Q(OldPc_q), .clr(Reset));  // open: en
  Register #(.width(32)) Instr (.D(Mem_dout), .en(controller_1_irwrite), .clk(clk_out), .Q(Instr_q), .clr(Reset));
  Register #(.width(32)) Data (.D(Mem_dout), .clk(clk_out), .Q(Data_q), .clr(Reset));  // open: en
  controller controller_1 (
    .zero(alu_1_zero), .op(Instr_q[6:0]), .funct3(Instr_q[14:12]), .funct7b5(Instr_q[30]), .clk(clk_out),
    .Reset(Reset), .PCWrite(controller_1_pcwrite), .AdrSrc(controller_1_adrsrc),
    .IRWrite(controller_1_irwrite), .MemWrite(controller_1_memwrite), .ResultSrc(controller_1_resultsrc),
    .ALUCtrl(controller_1_aluctrl), .ALUSrcB(controller_1_alusrcb), .ALUSrcA(controller_1_alusrca),
    .ImmSrc(controller_1_immsrc), .RegWrite(controller_1_regwrite));
  RegFile regfile_1 (
    .WD3(multiplexer_4_out), .CLK(clk_out), .A1(Instr_q[19:15]), .WE3(controller_1_regwrite),
    .A2(Instr_q[24:20]), .A3(Instr_q[11:7]), .Reset(Reset), .RD1(regfile_1_rd1), .RD2(regfile_1_rd2));
  Extend extend_1 (.immsrc(controller_1_immsrc), .instr(Instr_q[31:7]), .immext(extend_1_immext));
  Register #(.width(32)) A (.D(regfile_1_rd1), .clk(clk_out), .Q(A_q), .clr(Reset));  // open: en
  Register #(.width(32)) B (.D(regfile_1_rd2), .clk(clk_out), .Q(B_q), .clr(Reset));  // open: en
  Multiplexer #(.select(2), .width(32)) multiplexer_2 (
    .in0(register_1_q), .in1(OldPc_q), .in2(A_q), .out(multiplexer_2_out), .sel(controller_1_alusrca));  // open: in3
  Multiplexer #(.select(2), .width(32)) multiplexer_3 (
    .in0(B_q), .in1(extend_1_immext), .in2(32'h4), .out(multiplexer_3_out), .sel(controller_1_alusrcb));  // open: in3
  ALU alu_1 (
    .ALUControl(controller_1_aluctrl), .SrcA(multiplexer_2_out), .SrcB(multiplexer_3_out), .zero(alu_1_zero),
    .ALUResult(alu_1_aluresult));
  Register #(.width(32)) ALUOut (.D(alu_1_aluresult), .clk(clk_out), .Q(ALUOut_q), .clr(Reset));  // open: en
  Multiplexer #(.select(2), .width(32)) multiplexer_4 (
    .in0(ALUOut_q), .in1(Data_q), .in2(alu_1_aluresult), .out(multiplexer_4_out), .sel(controller_1_resultsrc));  // open: in3
  Comparator #(.width(32)) comparator_1 (.a(Instr_q), .b(32'h73), .eq(halt));  // open: gt, lt

  // Notes on the sheet:
  //   Pin used for halting Simulation
endmodule

module controller (
  input  zero,
  input  [6:0] op,
  input  [2:0] funct3,
  input  funct7b5,
  input  clk,
  input  Reset,
  output PCWrite,
  output AdrSrc,
  output IRWrite,
  output MemWrite,
  output [1:0] ResultSrc,
  output [2:0] ALUCtrl,
  output [1:0] ALUSrcB,
  output [1:0] ALUSrcA,
  output [1:0] ImmSrc,
  output RegWrite
);

  wire and_1_out, bitselector_1_out, maindec_1_branch, maindec_1_pcupdate;
  wire [1:0] maindec_1_aluop;

  BitSelector #(.width(7)) bitselector_1 (.in(op), .out(bitselector_1_out), .sel(3'b101));
  MainDec maindec_1 (
    .op(op), .clk(clk), .funct3(funct3), .Reset(Reset), .Branch(maindec_1_branch),
    .PCUpdate(maindec_1_pcupdate), .IRWrite(IRWrite), .MemWrite(MemWrite), .ResultSrc(ResultSrc),
    .ALUSrcB(ALUSrcB), .ALUSrcA(ALUSrcA), .AdrSrc(AdrSrc), .ALUOp(maindec_1_aluop), .RegWrite(RegWrite));
  ALUDec aludec_1 (
    .opb5(bitselector_1_out), .funct3(funct3), .funct7b5(funct7b5), .ALUOp(maindec_1_aluop),
    .ALUControl(ALUCtrl));
  InstrDecoder instrdecoder_1 (.op(op), .ImmSrc(ImmSrc));
  and and_1 (and_1_out, zero, maindec_1_branch);
  or or_1 (PCWrite, and_1_out, maindec_1_pcupdate);
endmodule

module MainDec (
  input  [6:0] op,
  input  clk,
  input  [2:0] funct3,
  input  Reset,
  output Branch,
  output PCUpdate,
  output IRWrite,
  output MemWrite,
  output [1:0] ResultSrc,
  output [1:0] ALUSrcB,
  output [1:0] ALUSrcA,
  output AdrSrc,
  output [1:0] ALUOp,
  output RegWrite
);

  wire [3:0] State_q, stateupdate_1_newstate;

  Register #(.width(4)) State (.D(stateupdate_1_newstate), .en(clk), .clk(Reset), .Q(State_q));  // open: clr
  StateUpdate stateupdate_1 (.State(State_q), .op(op), .newState(stateupdate_1_newstate));
  StateToOutput statetooutput_1 (
    .State(State_q), .Branch(Branch), .PCUpdate(PCUpdate), .IRWrite(IRWrite), .MemWrite(MemWrite),
    .ResultSrc(ResultSrc), .ALUSrcB(ALUSrcB), .ALUSrcA(ALUSrcA), .AdrSrc(AdrSrc), .ALUOp(ALUOp),
    .RegWrite(RegWrite));
endmodule

module ALUDec (
  input  opb5,
  input  [2:0] funct3,
  input  funct7b5,
  input  [1:0] ALUOp,
  output [2:0] ALUControl
);

  wire and_1_out;
  wire [2:0] multiplexer_1_out, multiplexer_2_out, multiplexer_3_out;

  and and_1 (and_1_out, opb5, funct7b5);
  Multiplexer #(.width(3)) multiplexer_1 (.in0(3'b000), .in1(3'b001), .out(multiplexer_1_out), .sel(and_1_out));
  Multiplexer #(.select(3), .width(3)) multiplexer_2 (
    .in0(multiplexer_1_out), .in2(3'b101), .in6(3'b011), .in7(3'b010), .out(multiplexer_2_out), .sel(funct3));  // open: in1, in3, in4, in5
  Multiplexer #(.width(3)) multiplexer_3 (.in0(3'b000), .in1(3'b001), .out(multiplexer_3_out), .sel(ALUOp[0]));
  Multiplexer #(.width(3)) multiplexer_4 (
    .in0(multiplexer_3_out), .in1(multiplexer_2_out), .out(ALUControl), .sel(ALUOp[1]));

  // Notes on the sheet:
  //   SLT
  //   OR
  //   AND
  //   Sub
  //   Add
endmodule

module InstrDecoder (
  input  [6:0] op,
  output [1:0] ImmSrc
);

  wire comparator_1_eq, comparator_2_eq, comparator_3_eq, comparator_4_eq, comparator_5_eq, comparator_6_eq,
       or_1_out, or_2_out;

  Comparator #(.width(7)) comparator_1 (.a(7'b0000011), .b(op), .eq(comparator_1_eq));  // open: gt, lt
  Comparator #(.width(7)) comparator_2 (.a(7'b0010011), .b(op), .eq(comparator_2_eq));  // open: gt, lt
  Comparator #(.width(7)) comparator_3 (.a(7'b1100111), .b(op), .eq(comparator_3_eq));  // open: gt, lt
  Comparator #(.width(7)) comparator_4 (.a(7'b0100011), .b(op), .eq(comparator_4_eq));  // open: gt, lt
  Comparator #(.width(7)) comparator_5 (.a(7'b1100011), .b(op), .eq(comparator_5_eq));  // open: gt, lt
  Comparator #(.width(7)) comparator_6 (.a(7'b1101111), .b(op), .eq(comparator_6_eq));  // open: gt, lt
  or or_1 (or_1_out, comparator_1_eq, comparator_2_eq);
  or or_2 (or_2_out, or_1_out, comparator_3_eq);
  Priority_Encoder #(.select(2)) priority_encoder_1 (
    .in0(or_2_out), .in1(comparator_4_eq), .in2(comparator_5_eq), .in3(comparator_6_eq), .out(ImmSrc));  // open: gs, en_out, en_in
endmodule

module StateToOutput (
  input  [3:0] State,
  output Branch,
  output PCUpdate,
  output IRWrite,
  output MemWrite,
  output [1:0] ResultSrc,
  output [1:0] ALUSrcB,
  output [1:0] ALUSrcA,
  output AdrSrc,
  output [1:0] ALUOp,
  output RegWrite
);

  Multiplexer #(.select(4), .width(14)) multiplexer_1 (
    .in0(14'ha6), .in1(14'h140), .in2(14'h240), .in3(14'h400), .in4(14'h2010), .in5(14'h408), .in6(14'h1200),
    .in7(14'h2000), .in8(14'h1240), .in9(14'h182), .in10(14'ha01), .in11({14{1'b0}}), .in12({14{1'b0}}),
    .in13({14{1'b0}}), .in14({14{1'b0}}), .in15({14{1'b0}}),
    .out({RegWrite, ALUOp, AdrSrc, ALUSrcA, ALUSrcB, ResultSrc, MemWrite, IRWrite, PCUpdate, Branch}),
    .sel(State));
endmodule

module StateUpdate (
  input  [3:0] State,
  input  [6:0] op,
  output [3:0] newState
);

  wire comparator_1_eq, comparator_2_eq, comparator_3_eq, comparator_4_eq, comparator_5_eq, comparator_6_eq,
       comparator_7_eq, comparator_8_eq, priority_encoder_1_out;
  wire [2:0] priority_encoder_2_out;
  wire [3:0] multiplexer_1_out, multiplexer_2_out;

  Comparator #(.width(7)) comparator_1 (.a(7'b0000011), .b(op), .eq(comparator_1_eq));  // open: gt, lt
  Comparator #(.width(7)) comparator_2 (.a(7'b0100011), .b(op), .eq(comparator_2_eq));  // open: gt, lt
  Priority_Encoder #(.select(1)) priority_encoder_1 (
    .in0(comparator_1_eq), .in1(comparator_2_eq), .out(priority_encoder_1_out));  // open: gs, en_out, en_in
  Multiplexer #(.width(4)) multiplexer_1 (
    .in0(4'b0011), .in1(4'b0101), .out(multiplexer_1_out), .sel(priority_encoder_1_out));
  Comparator #(.width(7)) comparator_3 (.a(7'b0000011), .b(op), .eq(comparator_3_eq));  // open: gt, lt
  Comparator #(.width(7)) comparator_4 (.a(7'b0100011), .b(op), .eq(comparator_4_eq));  // open: gt, lt
  Comparator #(.width(7)) comparator_5 (.a(7'b0110011), .b(op), .eq(comparator_5_eq));  // open: gt, lt
  Comparator #(.width(7)) comparator_6 (.a(7'b0010011), .b(op), .eq(comparator_6_eq));  // open: gt, lt
  Comparator #(.width(7)) comparator_7 (.a(7'b1101111), .b(op), .eq(comparator_7_eq));  // open: gt, lt
  Comparator #(.width(7)) comparator_8 (.a(7'b1100011), .b(op), .eq(comparator_8_eq));  // open: gt, lt
  Multiplexer #(.select(3), .width(4)) multiplexer_2 (
    .in0(4'b0010), .in1(4'b0010), .in2(4'b0110), .in3(4'b1000), .in4(4'b1001), .in5(4'b1010),
    .out(multiplexer_2_out), .sel(priority_encoder_2_out));  // open: in6, in7
  Priority_Encoder priority_encoder_2 (
    .in0(comparator_3_eq), .in1(comparator_4_eq), .in2(comparator_5_eq), .in3(comparator_6_eq),
    .in4(comparator_7_eq), .in5(comparator_8_eq), .out(priority_encoder_2_out));  // open: in6, in7, en_in, gs, en_out
  Multiplexer #(.select(4), .width(4)) multiplexer_3 (
    .in0(4'b0001), .in1(multiplexer_2_out), .in2(multiplexer_1_out), .in3(4'b0100), .in4(4'b0000),
    .in5(4'b0000), .in6(4'b0111), .in7(4'b0000), .in8(4'b0111), .in9(4'b0111), .in10(4'b0000),
    .out(newState), .sel(State));  // open: in11, in12, in13, in14, in15
endmodule

module ALU (
  input  [2:0] ALUControl,
  input  [31:0] SrcA,
  input  [31:0] SrcB,
  output zero,
  output [31:0] ALUResult
);

  wire bitselector_1_out, bitselector_2_out;
  wire [31:0] adder_1_out, and_1_out, bit_extender_1_out, multiplexer_1_out, not_1_out, or_1_out;

  BitSelector #(.width(3)) bitselector_1 (.in(ALUControl), .out(bitselector_1_out), .sel(2'b00));
  assign not_1_out = ~SrcB;  // NOT_Gate not_1, 32 bits wide
  Multiplexer #(.width(32)) multiplexer_1 (
    .in0(SrcB), .in1(not_1_out), .out(multiplexer_1_out), .sel(bitselector_1_out));
  assign and_1_out = SrcA & SrcB;  // AND_Gate and_1, 32 bits wide
  assign or_1_out = SrcA | SrcB;  // OR_Gate or_1, 32 bits wide
  Adder #(.width(32)) adder_1 (
    .a(SrcA), .b(multiplexer_1_out), .out(adder_1_out), .cin(bitselector_1_out));  // open: cout
  BitSelector #(.width(32)) bitselector_2 (.in(adder_1_out), .out(bitselector_2_out), .sel({5{1'b1}}));
  assign bit_extender_1_out = {{31{1'b0}}, bitselector_2_out};  // Bit_Extender bit_extender_1
  Multiplexer #(.select(3), .width(32)) multiplexer_2 (
    .in0(adder_1_out), .in1(adder_1_out), .in2(and_1_out), .in3(or_1_out), .in5(bit_extender_1_out),
    .out(ALUResult), .sel(ALUControl));  // open: in4, in6, in7
  Comparator #(.width(32)) comparator_1 (.a({32{1'b0}}), .b(ALUResult), .eq(zero));  // open: gt, lt
endmodule

module RegFile (
  input  [31:0] WD3,
  input  CLK,
  input  [4:0] A1,
  input  WE3,
  input  [4:0] A2,
  input  [4:0] A3,
  input  Reset,
  output [31:0] RD1,
  output [31:0] RD2
);

  wire and_1_out, and_2_out, and_3_out, and_4_out, and_5_out, and_6_out, and_7_out, and_8_out, and_9_out,
       and_10_out, and_11_out, and_12_out, and_13_out, and_14_out, and_15_out, and_16_out, and_17_out,
       and_18_out, and_19_out, and_20_out, and_21_out, and_22_out, and_23_out, and_24_out, and_25_out,
       and_26_out, and_27_out, and_28_out, and_29_out, and_30_out, and_31_out, demultiplexer_1_out1,
       demultiplexer_1_out2, demultiplexer_1_out3, demultiplexer_1_out4, demultiplexer_1_out5,
       demultiplexer_1_out6, demultiplexer_1_out7, demultiplexer_1_out8, demultiplexer_1_out9,
       demultiplexer_1_out10, demultiplexer_1_out11, demultiplexer_1_out12, demultiplexer_1_out13,
       demultiplexer_1_out14, demultiplexer_1_out15, demultiplexer_1_out16, demultiplexer_1_out17,
       demultiplexer_1_out18, demultiplexer_1_out19, demultiplexer_1_out20, demultiplexer_1_out21,
       demultiplexer_1_out22, demultiplexer_1_out23, demultiplexer_1_out24, demultiplexer_1_out25,
       demultiplexer_1_out26, demultiplexer_1_out27, demultiplexer_1_out28, demultiplexer_1_out29,
       demultiplexer_1_out30, demultiplexer_1_out31;
  wire [31:0] x1_q, x2_q, x3_q, x4_q, x5_q, x6_q, x7_q, x8_q, x9_q, x10_q, x11_q, x12_q, x13_q, x14_q, x15_q,
       x16_q, x17_q, x18_q, x19_q, x20_q, x21_q, x22_q, x23_q, x24_q, x25_q, x26_q, x27_q, x28_q, x29_q,
       x30_q, x31_q;

  Demultiplexer #(.select(5)) demultiplexer_1 (
    .out1(demultiplexer_1_out1), .out2(demultiplexer_1_out2), .out3(demultiplexer_1_out3),
    .out4(demultiplexer_1_out4), .out5(demultiplexer_1_out5), .out6(demultiplexer_1_out6),
    .out7(demultiplexer_1_out7), .out8(demultiplexer_1_out8), .out9(demultiplexer_1_out9),
    .out10(demultiplexer_1_out10), .out11(demultiplexer_1_out11), .out12(demultiplexer_1_out12),
    .out13(demultiplexer_1_out13), .out14(demultiplexer_1_out14), .out15(demultiplexer_1_out15),
    .out16(demultiplexer_1_out16), .out17(demultiplexer_1_out17), .out18(demultiplexer_1_out18),
    .out19(demultiplexer_1_out19), .out20(demultiplexer_1_out20), .out21(demultiplexer_1_out21),
    .out22(demultiplexer_1_out22), .out23(demultiplexer_1_out23), .out24(demultiplexer_1_out24),
    .out25(demultiplexer_1_out25), .out26(demultiplexer_1_out26), .out27(demultiplexer_1_out27),
    .out28(demultiplexer_1_out28), .out29(demultiplexer_1_out29), .out30(demultiplexer_1_out30),
    .out31(demultiplexer_1_out31), .in(1'b1), .sel(A3));  // open: out0
  Register #(.width(32)) x8 (.D(WD3), .en(and_1_out), .clk(CLK), .Q(x8_q), .clr(Reset));
  and and_1 (and_1_out, demultiplexer_1_out8, WE3);
  Register #(.width(32)) x16 (.D(WD3), .en(and_2_out), .clk(CLK), .Q(x16_q), .clr(Reset));
  and and_2 (and_2_out, demultiplexer_1_out16, WE3);
  Register #(.width(32)) x24 (.D(WD3), .en(and_3_out), .clk(CLK), .Q(x24_q), .clr(Reset));
  and and_3 (and_3_out, demultiplexer_1_out24, WE3);
  and and_4 (and_4_out, demultiplexer_1_out1, WE3);
  and and_5 (and_5_out, demultiplexer_1_out9, WE3);
  and and_6 (and_6_out, demultiplexer_1_out17, WE3);
  and and_7 (and_7_out, demultiplexer_1_out25, WE3);
  Register #(.width(32)) x1 (.D(WD3), .en(and_4_out), .clk(CLK), .Q(x1_q), .clr(Reset));
  Register #(.width(32)) x9 (.D(WD3), .en(and_5_out), .clk(CLK), .Q(x9_q), .clr(Reset));
  Register #(.width(32)) x17 (.D(WD3), .en(and_6_out), .clk(CLK), .Q(x17_q), .clr(Reset));
  Register #(.width(32)) x25 (.D(WD3), .en(and_7_out), .clk(CLK), .Q(x25_q), .clr(Reset));
  Register #(.width(32)) x2 (.D(WD3), .en(and_8_out), .clk(CLK), .Q(x2_q), .clr(Reset));
  and and_8 (and_8_out, demultiplexer_1_out2, WE3);
  Register #(.width(32)) x10 (.D(WD3), .en(and_9_out), .clk(CLK), .Q(x10_q), .clr(Reset));
  and and_9 (and_9_out, demultiplexer_1_out10, WE3);
  Register #(.width(32)) x18 (.D(WD3), .en(and_10_out), .clk(CLK), .Q(x18_q), .clr(Reset));
  and and_10 (and_10_out, demultiplexer_1_out18, WE3);
  Register #(.width(32)) x26 (.D(WD3), .en(and_11_out), .clk(CLK), .Q(x26_q), .clr(Reset));
  and and_11 (and_11_out, demultiplexer_1_out26, WE3);
  and and_12 (and_12_out, demultiplexer_1_out3, WE3);
  and and_13 (and_13_out, demultiplexer_1_out11, WE3);
  and and_14 (and_14_out, demultiplexer_1_out19, WE3);
  and and_15 (and_15_out, demultiplexer_1_out27, WE3);
  Register #(.width(32)) x3 (.D(WD3), .en(and_12_out), .clk(CLK), .Q(x3_q), .clr(Reset));
  Register #(.width(32)) x11 (.D(WD3), .en(and_13_out), .clk(CLK), .Q(x11_q), .clr(Reset));
  Register #(.width(32)) x19 (.D(WD3), .en(and_14_out), .clk(CLK), .Q(x19_q), .clr(Reset));
  Register #(.width(32)) x27 (.D(WD3), .en(and_15_out), .clk(CLK), .Q(x27_q), .clr(Reset));
  Register #(.width(32)) x4 (.D(WD3), .en(and_16_out), .clk(CLK), .Q(x4_q), .clr(Reset));
  and and_16 (and_16_out, demultiplexer_1_out4, WE3);
  Register #(.width(32)) x12 (.D(WD3), .en(and_17_out), .clk(CLK), .Q(x12_q), .clr(Reset));
  and and_17 (and_17_out, demultiplexer_1_out12, WE3);
  Register #(.width(32)) x20 (.D(WD3), .en(and_18_out), .clk(CLK), .Q(x20_q), .clr(Reset));
  and and_18 (and_18_out, demultiplexer_1_out20, WE3);
  Register #(.width(32)) x28 (.D(WD3), .en(and_19_out), .clk(CLK), .Q(x28_q), .clr(Reset));
  and and_19 (and_19_out, demultiplexer_1_out28, WE3);
  Register #(.width(32)) x5 (.D(WD3), .en(and_20_out), .clk(CLK), .Q(x5_q), .clr(Reset));
  and and_20 (and_20_out, demultiplexer_1_out5, WE3);
  Register #(.width(32)) x13 (.D(WD3), .en(and_21_out), .clk(CLK), .Q(x13_q), .clr(Reset));
  and and_21 (and_21_out, demultiplexer_1_out13, WE3);
  Register #(.width(32)) x21 (.D(WD3), .en(and_22_out), .clk(CLK), .Q(x21_q), .clr(Reset));
  and and_22 (and_22_out, demultiplexer_1_out21, WE3);
  Register #(.width(32)) x29 (.D(WD3), .en(and_23_out), .clk(CLK), .Q(x29_q), .clr(Reset));
  and and_23 (and_23_out, demultiplexer_1_out29, WE3);
  and and_24 (and_24_out, demultiplexer_1_out6, WE3);
  and and_25 (and_25_out, demultiplexer_1_out14, WE3);
  and and_26 (and_26_out, demultiplexer_1_out22, WE3);
  and and_27 (and_27_out, demultiplexer_1_out30, WE3);
  Register #(.width(32)) x6 (.D(WD3), .en(and_24_out), .clk(CLK), .Q(x6_q), .clr(Reset));
  Register #(.width(32)) x14 (.D(WD3), .en(and_25_out), .clk(CLK), .Q(x14_q), .clr(Reset));
  Register #(.width(32)) x22 (.D(WD3), .en(and_26_out), .clk(CLK), .Q(x22_q), .clr(Reset));
  Register #(.width(32)) x30 (.D(WD3), .en(and_27_out), .clk(CLK), .Q(x30_q), .clr(Reset));
  Register #(.width(32)) x7 (.D(WD3), .en(and_28_out), .clk(CLK), .Q(x7_q), .clr(Reset));
  and and_28 (and_28_out, demultiplexer_1_out7, WE3);
  Register #(.width(32)) x15 (.D(WD3), .en(and_29_out), .clk(CLK), .Q(x15_q), .clr(Reset));
  and and_29 (and_29_out, demultiplexer_1_out15, WE3);
  Register #(.width(32)) x23 (.D(WD3), .en(and_30_out), .clk(CLK), .Q(x23_q), .clr(Reset));
  and and_30 (and_30_out, demultiplexer_1_out23, WE3);
  Register #(.width(32)) x31 (.D(WD3), .en(and_31_out), .clk(CLK), .Q(x31_q), .clr(Reset));
  and and_31 (and_31_out, demultiplexer_1_out31, WE3);
  Multiplexer #(.select(5), .width(32)) multiplexer_1 (
    .in0({32{1'b0}}), .in1(x1_q), .in2(x2_q), .in3(x3_q), .in4(x4_q), .in5(x5_q), .in6(x6_q), .in7(x7_q),
    .in8(x8_q), .in9(x9_q), .in10(x10_q), .in11(x11_q), .in12(x12_q), .in13(x13_q), .in14(x14_q),
    .in15(x15_q), .in16(x16_q), .in17(x17_q), .in18(x18_q), .in19(x19_q), .in20(x20_q), .in21(x21_q),
    .in22(x22_q), .in23(x23_q), .in24(x24_q), .in25(x25_q), .in26(x26_q), .in27(x27_q), .in28(x28_q),
    .in29(x29_q), .in30(x30_q), .in31(x31_q), .out(RD1), .sel(A1));
  Multiplexer #(.select(5), .width(32)) multiplexer_2 (
    .in0({32{1'b0}}), .in1(x1_q), .in2(x2_q), .in3(x3_q), .in4(x4_q), .in5(x5_q), .in6(x6_q), .in7(x7_q),
    .in8(x8_q), .in9(x9_q), .in10(x10_q), .in11(x11_q), .in12(x12_q), .in13(x13_q), .in14(x14_q),
    .in15(x15_q), .in16(x16_q), .in17(x17_q), .in18(x18_q), .in19(x19_q), .in20(x20_q), .in21(x21_q),
    .in22(x22_q), .in23(x23_q), .in24(x24_q), .in25(x25_q), .in26(x26_q), .in27(x27_q), .in28(x28_q),
    .in29(x29_q), .in30(x30_q), .in31(x31_q), .out(RD2), .sel(A2));

  // Notes on the sheet:
  //   Zero Register is hardwired to 0
endmodule

module Extend (
  input  [1:0] immsrc,
  input  [24:0] instr,
  output [31:0] immext
);

  wire [11:0] bit_extender_2_out;
  wire [19:0] bit_extender_1_out;

  // NoConnect on instr[12:0]
  assign bit_extender_1_out = {{19{instr[24]}}, instr[24]};  // Bit_Extender bit_extender_1
  assign bit_extender_2_out = {{11{instr[24]}}, instr[24]};  // Bit_Extender bit_extender_2
  Multiplexer #(.select(2), .width(32)) multiplexer_1 (
    .in0({bit_extender_1_out, instr[24:13]}), .in1({bit_extender_1_out, instr[24:18], instr[4:0]}),
    .in2({bit_extender_1_out, instr[0], instr[23:18], instr[4:1], 1'b0}),
    .in3({bit_extender_2_out, instr[12:5], instr[13], instr[23:14], 1'b0}), .out(immext), .sel(immsrc));
endmodule
